// Logisim project 4-bit alu.circ as structural Verilog: 1 circuit, main circuit main
module main (
  input  [3:0] number_a,
  input  [3:0] number_b,
  input  [2:0] ALU_control,
  output [3:0] out_4,
  output [3:0] out_5,
  output [3:0] out_6,
  output [3:0] out_7,
  output [3:0] out_8
);

  wire [3:0] multiplexer_1_out, not_1_out;

  assign not_1_out = ~number_b;  // NOT_Gate not_1, 4 bits wide
  Multiplexer #(.width(4), .enable("false")) multiplexer_1 (
    .in0(number_b), .in1(not_1_out), .out(multiplexer_1_out), .sel(ALU_control[0]));
  Adder #(.width(4)) adder_1 (.a(number_a), .b(multiplexer_1_out), .out(out_4), .cin(ALU_control[0]));  // open: cout
  assign out_6 = number_a & number_b;  // AND_Gate and_1, 4 bits wide
  assign out_7 = number_a | number_b;  // OR_Gate or_1, 4 bits wide
  assign out_8 = number_a ^ number_b;  // XOR_Gate xor_1, 4 bits wide
  Multiplexer #(.select(3), .width(4), .enable("false")) multiplexer_2 (
    .in0(out_4), .in1(out_4), .in2(out_6), .in3(out_7), .in4(out_8), .out(out_5), .sel(ALU_control));  // open: in5, in6, in7
endmodule
